// Logisim project karnaugh map 2.circ as structural Verilog: 1 circuit, main circuit main
module main (
  input  in_1,
  input  in_2,
  input  in_3,
  input  in_4,
  output \F_A_B_C_D__Σm_0_2_5_7_8_10_13_15__before_minimization 
);

  wire m0_out, m2_out, m5_out, m7_out, m8_out, m10_out, m13_out, m15_out, not_1_out, not_2_out, not_3_out,
       not_4_out;

  not not_1 (not_1_out, in_1);
  not not_2 (not_2_out, in_2);
  not not_3 (not_3_out, in_3);
  not not_4 (not_4_out, in_4);
  and m0 (m0_out, not_1_out, not_2_out, not_3_out, not_4_out);
  and m2 (m2_out, not_1_out, not_2_out, in_3, not_4_out);
  and m5 (m5_out, not_1_out, in_2, in_3, in_4);
  and m7 (m7_out, in_1, not_2_out, not_3_out, not_4_out);
  and m8 (m8_out, in_1, not_2_out, not_3_out, not_4_out);
  and m10 (m10_out, in_1, not_3_out, in_3, not_4_out);
  and m13 (m13_out, in_1, in_2, not_3_out, in_4);
  and m15 (m15_out, in_1, in_2, in_3, in_4);
  or or_1 (\F_A_B_C_D__Σm_0_2_5_7_8_10_13_15__before_minimization , m0_out, m2_out, m5_out, m7_out, m8_out, m10_out, m13_out, m15_out);
endmodule
